# Fritzing sketch WiFiEnvironmentMonitorOutdor_Sensors (saved by Fritzing 0.9.3b)

parts:
  WeMos_D1_Mini2 = WeMos D1 Mini
  DHT1 = DHT22 Humidity and Temperature Sensor
  Part1 = BH1750
  R1 = Resistor [tolerance=±5% resistance=470k package="0805 [SMD]"]
  R2 = Resistor [tolerance=±5% resistance=100k package="0805 [SMD]"]
  Part2 = Barometric Pressure Sensor - BMP180 Breakout (GY-68)

nets:
  N1: WeMos_D1_Mini2.5V, R1.Pin_0
  N2: WeMos_D1_Mini2.A0, R1.Pin_1, R2.Pin_0
  N3: WeMos_D1_Mini2.D0, WeMos_D1_Mini2.RST
  N4: WeMos_D1_Mini2.D1, DHT1.DATA
  N5: WeMos_D1_Mini2.D2, Part1.SCL, Part2.SCL
  N6: WeMos_D1_Mini2.D4, Part1.SDA, Part2.SDA
  VCC: WeMos_D1_Mini2.D6, DHT1.VDD, Part1.VCC, Part2.VCC
  GND: WeMos_D1_Mini2.G, DHT1.GND, Part1.GND, R2.Pin_1, Part2.GND

custom parts:
  BH1750: Light Sensor
